// Logisim project Lab3.circ as structural Verilog: 4 circuits, main circuit P1
module P1 (
  input  in_1,
  input  in_2,
  input  in_3,
  output out_4,
  output out_5,
  output out_6,
  output out_7
);

  wire and_1_out, and_2_out, and_3_out, clock_1_out, nor_1_out, nor_2_out, not_1_out, not_2_out;

  Clock clock_1 (.out(clock_1_out));
  not not_1 (not_1_out, in_1);
  nor nor_1 (nor_1_out, not_1_out, in_2);
  nor nor_2 (nor_2_out, in_2, in_1);
  and and_1 (and_1_out, clock_1_out, clock_1_out);
  not not_2 (not_2_out, in_3);
  nor nor_3 (out_4, nor_1_out, out_5);
  nor nor_4 (out_5, out_4, nor_2_out);
  and and_2 (and_2_out, in_3, and_1_out);
  and and_3 (and_3_out, and_1_out, not_2_out);
  nor nor_5 (out_6, and_2_out, out_7);
  nor nor_6 (out_7, out_6, and_3_out);
endmodule

module P2 (
  input  in_1,
  input  in_2,
  input  in_3,
  input  in_4,
  input  in_5,
  input  in_6,
  output out_7,
  output out_8,
  output out_9,
  output out_10
);

  wire d_ff_1_q, d_ff_2_q, d_ff_3_q, d_ff_4_q;

  D_Flip_Flop d_ff_1 (.D(in_1), .clk(in_5), .Q(d_ff_1_q));  // open: Qn, preset, reset
  and and_1 (out_7, in_6, d_ff_1_q);
  D_Flip_Flop d_ff_2 (.D(in_2), .clk(in_5), .Q(d_ff_2_q));  // open: Qn, preset, reset
  and and_2 (out_8, in_6, d_ff_2_q);
  D_Flip_Flop d_ff_3 (.D(in_3), .clk(in_5), .Q(d_ff_3_q));  // open: Qn, preset, reset
  D_Flip_Flop d_ff_4 (.D(in_4), .clk(in_5), .Q(d_ff_4_q));  // open: Qn, preset, reset
  and and_3 (out_9, in_6, d_ff_3_q);
  and and_4 (out_10, in_6, d_ff_4_q);
endmodule

module p3 (
  input  in_1,
  input  in_2,
  input  in_3,
  input  in_4,
  input  [2:0] in_5,
  output out_6,
  output out_7,
  output out_8
);

  wire and_1_out, and_2_out, and_3_out, and_4_out, clock_1_out, d_ff_1_q, d_ff_2_q, d_ff_3_q, d_ff_4_q,
       d_ff_5_q, d_ff_6_q, d_ff_7_q, d_ff_8_q, d_ff_9_q, d_ff_10_q, d_ff_11_q, d_ff_12_q, d_ff_13_q,
       d_ff_14_q, d_ff_15_q, decoder_1_out0, decoder_1_out1, decoder_1_out2, decoder_1_out3, decoder_1_out4;

  Clock clock_1 (.out(clock_1_out));
  Decoder #(.select(3)) decoder_1 (
    .out0(decoder_1_out0), .out1(decoder_1_out1), .out2(decoder_1_out2), .out3(decoder_1_out3),
    .out4(decoder_1_out4), .sel(in_5), .en(in_4));  // open: out5, out6, out7
  and and_1 (and_1_out, decoder_1_out0, clock_1_out);
  and and_2 (and_2_out, decoder_1_out1, clock_1_out);
  and and_3 (and_3_out, decoder_1_out2, clock_1_out);
  and and_4 (and_4_out, decoder_1_out3, clock_1_out);
  // AND_Gate and_5 has open pins: in0=clock_1_out, in1=decoder_1_out4, out=open
  D_Flip_Flop d_ff_1 (.D(in_1), .clk(and_1_out), .Q(d_ff_1_q));  // open: Qn, preset, reset
  D_Flip_Flop d_ff_2 (.D(in_1), .clk(and_2_out), .Q(d_ff_2_q));  // open: Qn, preset, reset
  D_Flip_Flop d_ff_3 (.D(in_1), .clk(and_3_out), .Q(d_ff_3_q));  // open: Qn, preset, reset
  D_Flip_Flop d_ff_4 (.D(in_1), .clk(and_4_out), .Q(d_ff_4_q));  // open: Qn, preset, reset
  D_Flip_Flop d_ff_5 (.D(in_1), .clk(decoder_1_out4), .Q(d_ff_5_q));  // open: Qn, preset, reset
  Multiplexer #(.select(3)) multiplexer_1 (
    .in0(d_ff_1_q), .in1(d_ff_2_q), .in2(d_ff_3_q), .in3(d_ff_4_q), .in4(d_ff_5_q), .out(out_6), .sel(in_5));  // open: in5, in6, in7
  D_Flip_Flop d_ff_6 (.D(in_2), .clk(and_1_out), .Q(d_ff_6_q));  // open: Qn, preset, reset
  D_Flip_Flop d_ff_7 (.D(in_2), .clk(and_2_out), .Q(d_ff_7_q));  // open: Qn, preset, reset
  D_Flip_Flop d_ff_8 (.D(in_2), .clk(and_3_out), .Q(d_ff_8_q));  // open: Qn, preset, reset
  D_Flip_Flop d_ff_9 (.D(in_2), .clk(and_4_out), .Q(d_ff_9_q));  // open: Qn, preset, reset
  D_Flip_Flop d_ff_10 (.D(in_2), .clk(decoder_1_out4), .Q(d_ff_10_q));  // open: Qn, preset, reset
  Multiplexer #(.select(3)) multiplexer_2 (
    .in0(d_ff_6_q), .in1(d_ff_7_q), .in2(d_ff_8_q), .in3(d_ff_9_q), .in4(d_ff_10_q), .out(out_7), .sel(in_5));  // open: in5, in6, in7
  D_Flip_Flop d_ff_11 (.D(in_3), .clk(and_1_out), .Q(d_ff_11_q));  // open: Qn, preset, reset
  D_Flip_Flop d_ff_12 (.D(in_3), .clk(and_2_out), .Q(d_ff_12_q));  // open: Qn, preset, reset
  D_Flip_Flop d_ff_13 (.D(in_3), .clk(and_3_out), .Q(d_ff_13_q));  // open: Qn, preset, reset
  D_Flip_Flop d_ff_14 (.D(in_3), .clk(and_4_out), .Q(d_ff_14_q));  // open: Qn, preset, reset
  D_Flip_Flop d_ff_15 (.D(in_3), .clk(decoder_1_out4), .Q(d_ff_15_q));  // open: Qn, preset, reset
  Multiplexer #(.select(3)) multiplexer_3 (
    .in0(d_ff_11_q), .in1(d_ff_12_q), .in2(d_ff_13_q), .in3(d_ff_14_q), .in4(d_ff_15_q), .out(out_8),
    .sel(in_5));  // open: in5, in6, in7
endmodule

module p4 (
  input  [7:0] in_1,
  input  [7:0] in_2,
  input  in_3,
  input  in_4,
  input  [1:0] in_5,
  output [7:0] out_6,
  output [7:0] out_7
);

  wire and_1_out, and_2_out, and_3_out, and_4_out, clock_1_out, decoder_1_out0, decoder_1_out1,
       decoder_1_out2, decoder_1_out3;
  wire [7:0] register_1_q, register_2_q, register_3_q, register_4_q;

  Decoder #(.select(2)) decoder_1 (
    .out0(decoder_1_out0), .out1(decoder_1_out1), .out2(decoder_1_out2), .out3(decoder_1_out3), .sel(in_5),
    .en(in_4));
  and and_1 (and_1_out, in_3, decoder_1_out0);
  and and_2 (and_2_out, in_3, decoder_1_out1);
  and and_3 (and_3_out, in_3, decoder_1_out2);
  and and_4 (and_4_out, in_3, decoder_1_out3);
  Register register_1 (.D(in_2), .en(and_1_out), .clk(clock_1_out), .Q(register_1_q));  // open: clr
  Register register_2 (.D(in_2), .en(and_2_out), .clk(clock_1_out), .Q(register_2_q));  // open: clr
  Clock clock_1 (.out(clock_1_out));
  Multiplexer #(.select(2), .width(8)) multiplexer_1 (
    .in0(register_2_q), .in1(register_1_q), .out(out_6), .sel(in_5));  // open: in2, in3
  Register register_3 (.D(in_1), .en(and_3_out), .clk(clock_1_out), .Q(register_3_q));  // open: clr
  Register register_4 (.D(in_1), .en(and_4_out), .clk(clock_1_out), .Q(register_4_q));  // open: clr
  Multiplexer #(.select(2), .width(8)) multiplexer_2 (
    .in0(register_4_q), .in1(register_3_q), .out(out_7), .sel(in_5));  // open: in2, in3
endmodule
